# Fritzing sketch schematics (saved by Fritzing 0.9.3b)
breadboards: 1

parts:
  Raspberry_Pi_Zero1 = Raspberry Pi Zero
  J1 = Basic Servo
  S1 = Pushbutton [package="[THT]"]
  J2 = Basic Servo
  VCC1 = Battery block 9V
  Part1 = Breadboard Power Supply Board SMD
  J3 = Infrared Proximity Sensor
  J4 = Infrared Proximity Sensor
  J5 = Infrared Proximity Sensor
  Part2 = Adafruit ADS1115 16Bit I2C ADC [part_number="Adafruit #1085"]
  hc-sr1 = hc-sr04
  R2 = Resistor [tolerance=±5% resistance=330 package=THT]
  R3 = Resistor [tolerance=±5% resistance=470 package=THT]
  LED1 = LED - 5mm [color="Infrared (850nm)" package="5 mm [THT]"]  # not connected
  R4 = Photocell (LDR) [package=THT]  # not connected

nets:
  N1: Raspberry_Pi_Zero1.GPIO2, Part2.SDA
  N2: Raspberry_Pi_Zero1.GPIO3, Part2.SCL
  N3: Raspberry_Pi_Zero1.GPIO4, hc-sr1.Trig
  N4: Raspberry_Pi_Zero1.GPIO17, J1.pulse
  GND: Raspberry_Pi_Zero1.GPIO13, Raspberry_Pi_Zero1.GND, J1.gnd, S1.Pin_1, S1.Pin_2, S1.Pin_3, S1.Pin_4, J2.gnd, VCC1.-, Part1.GND, J3.GND, J4.GND, J5.GND, Part2.GND, hc-sr1.GND, R3.Pin_1
  VCC: Raspberry_Pi_Zero1.GPIO18, J1.vcc, J2.vcc, J2.pulse, Part1.VCC, J3.Vcc, J4.Vcc, J5.Vcc, Part2.VDD, hc-sr1.VCC
  N5: Raspberry_Pi_Zero1.GPIO14, R2.Pin_0
  N6: VCC1.+, Part1.VIN
  N7: J3.Vout, Part2.AIN0
  N8: J4.Vout, Part2.AIN2
  N9: J5.Vout, Part2.AIN1
  N10: hc-sr1.Echo, R2.Pin_1, R3.Pin_0

notes:
  5V
  FRONT
  LEFT
  RIGHT

custom parts:
  Adafruit ADS1115 16Bit I2C ADC: For microcontrollers without an analog-to-digital converter or when you want a higher-precision ADC, the ADS1115 provides 16-bit precision at 860 samples/second over I2C. The chip can be configured as 4 single-ended input channels, or two differential channels. As a nice bonus, it even includes a programmable gain amplifier, up to x16, to help boost up smaller single/differential signals to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
